# Fritzing sketch sherman (saved by Fritzing 0.9.3b)
breadboards: 1

parts:
  Componente4 = Arduino XBee Shield
  Componente5 = Bluetooth Module Breakout - Roving Networks (RN-41)
  U3 = L298 [package=multiwatt15_6400bgheatsink]
  U4 = L298 [package=multiwatt15_6400bgheatsink]
  M1 = DC Motor
  M2 = DC Motor
  M3 = Stepper Motor - Bipolar
  U5 = V_REG_LD1117VXX [package=78xxl]
  VCC2 = Battery  # not connected
  VCC1 = Battery

nets:
  N1: Componente4.D6, U3.IN1
  GND: Componente4.GND, U3.GND, U4.GND, M1.pin_1, M2.pin_1, M3.C, M3.D, U5.GND, VCC1.-
  N2: Componente4.D8, U4.IN4
  N3: Componente4.D7, U3.IN2
  N4: Componente4.D9, U4.IN3
  N5: Componente4.D10, U4.IN1
  N6: Componente4.D11, U4.IN2
  N7: Componente4.N$20, Componente5.UARTRX
  N8: Componente4.N$28, Componente5.VCC
  N9: Componente4.N$32, Componente5.UARTTX
  N10: Componente4.N$41, Componente5.GND
  N11: Componente4.N$45, Componente5.UARTRTS
  N12: Componente4.N$53, Componente5.RESET
  N13: Componente4.N$57, Componente5.UARTCTS
  N14: Componente4.N$65, Componente5.SPICLK
  N15: Componente4.N$69, Componente5.PIO2
  N16: Componente4.N$77, Componente5.PIO7
  N17: Componente4.N$81, Componente5.PIO3
  N18: Componente4.N$89, Componente5.PIO6
  N19: Componente4.N$93, Componente5.PIO5
  N20: Componente4.N$101, Componente5.SPIMOSI
  N21: Componente4.N$105, Componente5.PIO4
  N22: Componente4.N$113, Componente5.PIO10
  N23: Componente4.N$117, Componente5.SPICSB
  N24: Componente4.N$125, Componente5.PIO11
  N25: Componente4.N$129, Componente5.SPIMISO
  N26: Componente4.N$137, Componente5.10
  N27: U3.CSA, U5.OUT
  N28: U3.OUT1, M3.B
  N29: U3.OUT2, M3.A

notes:
  batería de 12 volts
  motor sierra]
  baterías 9 volts
  motores ruedas
